# Fritzing sketch DC-Motor (saved by Fritzing 0.9.4)
breadboards: 1

parts:
  Bauteil1 = Arduino Uno (Rev3)
  IC1 = L293D [package=THT]
  M1 = DC Motor
  PSU1 = Adjustable Breadboard Power Supply  # not connected

nets:
  N1: Bauteil1.GND, IC1.0V
  N2: Bauteil1.D3_PWM, IC1.In_2
  N3: Bauteil1.D4, IC1.In_1
  N4: Bauteil1.D5_PWM, IC1.Enable_1
  N5: IC1.Out_1_(_Controlled_by_Enable_1_), M1.pin_2
  N6: IC1.Out_2_(_Controlled_by_Enable_1_), M1.pin_1
