# Fritzing sketch ultrasonic (saved by Fritzing 0.9.4)
breadboards: 1

parts:
  Bauteil1 = Arduino Uno (Rev3)
  HC-SR04_Sensor_1 = HC-SR04 Ultrasonic Distance Sensor
  LED1 = LED - 5mm [color="Red (633nm)" package="5 mm [THT]"]
  LED2 = LED - 5mm [color="Yellow (595nm)" package="5 mm [THT]"]
  LED3 = LED - 5mm [color="Green (555nm)" package="5 mm [THT]"]
  R1 = Resistor [tolerance=±5% resistance=1k package=THT]
  R2 = Resistor [tolerance=±5% resistance=1k package=THT]
  R3 = Resistor [tolerance=±5% resistance=1k package=THT]

nets:
  N1: Bauteil1.D8, HC-SR04_Sensor_1.ECHO
  N2: Bauteil1.D9_PWM, HC-SR04_Sensor_1.TRIG
  GND: Bauteil1.GND, HC-SR04_Sensor_1.GND, LED1.cathode, LED2.cathode, LED3.cathode
  N3: Bauteil1.D2, R3.Pin_1
  N4: Bauteil1.D3_PWM, R2.Pin_1
  N5: Bauteil1.D4, R1.Pin_1
  5V: Bauteil1.5V, HC-SR04_Sensor_1.VCC
  N6: LED1.anode, R1.Pin_0
  N7: LED2.anode, R2.Pin_0
  N8: LED3.anode, R3.Pin_0
