# Fritzing sketch ultrasonic (saved by Fritzing 0.9.4)

parts:
  Bauteil1 = Arduino Uno (Rev3)
  HC-SR04_Sensor_1 = HC-SR04 Ultrasonic Distance Sensor

nets:
  N1: Bauteil1.D8, HC-SR04_Sensor_1.ECHO
  N2: Bauteil1.D9_PWM, HC-SR04_Sensor_1.TRIG
  GND: Bauteil1.GND, HC-SR04_Sensor_1.GND
  5V: Bauteil1.5V, HC-SR04_Sensor_1.VCC
